# Fritzing sketch plant_schematic (saved by Fritzing 0.9.0b)
breadboards: 1

parts:
  IC1 = attiny85 [package=dip]
  R1 = Resistor [tolerance=±5% resistance=10k package=THT]
  Q1_BC547B_NPN = NPN-Transistor [package="TO92 [THT]"]
  PUMP = DC Motor
  Q2_2N3904_NPN = NPN-Transistor [package="TO92 [THT]"]
  Piezo = Piezo Speaker
  LED1 = LED - 5mm [color="Green (565nm)" package="5 mm [THT]"]
  R3 = Resistor [tolerance=±5% resistance=220 package=THT]
  LED2 = LED - 5mm [color="Red (633nm)" package="5 mm [THT]"]
  R4 = Resistor [tolerance=±5% resistance=220 package=THT]
  S1 = Pushbutton [package="[THT]"]
  3xAA_1_5V = DC Power [voltage=4.5]
  MOISTURE_SENSOR = mystery part, 3 pins [chip_label=?]
  TANK_WATER_LEVEL = mystery part, 2 pins [chip_label=?]
  D3_1N4007 = Diode [package=diode-1n4001]
  J2 = AVR ISP 6 Pin [package=2x3_lock]
  S2 = Toggle Switch [package=THT]
  R5 = Resistor [tolerance=±5% resistance=1k package=THT]
  R12 = Resistor [tolerance=±5% resistance=1k package=THT]

nets:
  N1: IC1.Pin_1, J2.5
  N2: IC1.Pin_2, MOISTURE_SENSOR.pin1
  N3: IC1.Pin_3, R1.Pin_1, TANK_WATER_LEVEL.pin2
  GND: IC1.Pin_4, R1.Pin_0, Q1_BC547B_NPN.E, Piezo.pin2, LED2.cathode, 3xAA_1_5V.V-, MOISTURE_SENSOR.pin3, J2.6
  N4: IC1.Pin_5, J2.4, R5.Pin_0
  N5: IC1.Pin_6, Piezo.pin1, R4.Pin_1
  N6: IC1.Pin_7, J2.3, R12.Pin_0
  4.5V: IC1.Pin_8, PUMP.pin_1, Q2_2N3904_NPN.C, R3.Pin_0, S1.Pin_3, S1.Pin_4, D3_1N4007.C, J2.2, S2.L2
  N7: Q1_BC547B_NPN.B, S1.Pin_1, S1.Pin_2, R12.Pin_1
  N8: Q1_BC547B_NPN.C, PUMP.pin_2, LED1.cathode, D3_1N4007.A
  sensor_power: Q2_2N3904_NPN.E, MOISTURE_SENSOR.pin2, TANK_WATER_LEVEL.pin1
  N9: Q2_2N3904_NPN.B, R5.Pin_1
  N10: LED1.anode, R3.Pin_1
  N11: LED2.anode, R4.Pin_0
  N12: 3xAA_1_5V.V+, S2.COM

notes:
  PlantBartender, Measures soil moisture and activates a water pump when needed. A. Roots <ando@sqroot.eu>, 4
